# Fritzing sketch calculator (saved by Fritzing 1.0.1rc)
circuit board: 10.667cm x 11.0611cm
breadboards: 2

parts:
  Mod1 = Raspberry Pi Pico
  SW1 = DIP SWITCH [package=dipswitch-02]
  SW2 = DIP SWITCH [package=dipswitch-02]
  元件1 = Arduino Nano (Rev3.0) (ICSP)
  LCD1 = TFT 1.8 inch 160x128 w SD
  S1 = Pushbutton [package="[THT]"]
  S2 = Pushbutton [package="[THT]"]
  S3 = Pushbutton [package="[THT]"]
  S4 = Pushbutton [package="[THT]"]
  S5 = Pushbutton [package="[THT]"]
  S6 = Pushbutton [package="[THT]"]
  S7 = Pushbutton [package="[THT]"]
  S8 = Pushbutton [package="[THT]"]
  S9 = Pushbutton [package="[THT]"]
  S10 = Pushbutton [package="[THT]"]
  S11 = Pushbutton [package="[THT]"]
  S12 = Pushbutton [package="[THT]"]
  S13 = Pushbutton [package="[THT]"]
  S14 = Pushbutton [package="[THT]"]
  S15 = Pushbutton [package="[THT]"]
  S16 = Pushbutton [package="[THT]"]
  S17 = Pushbutton [package="[THT]"]
  S18 = Pushbutton [package="[THT]"]
  S19 = Pushbutton [package="[THT]"]
  S20 = Pushbutton [package="[THT]"]
  S21 = Pushbutton [package="[THT]"]
  S22 = Pushbutton [package="[THT]"]
  S23 = Pushbutton [package="[THT]"]
  S24 = Pushbutton [package="[THT]"]
  S25 = Pushbutton [package="[THT]"]
  S26 = Pushbutton [package="[THT]"]
  S27 = Pushbutton [package="[THT]"]
  S28 = Pushbutton [package="[THT]"]
  S29 = Pushbutton [package="[THT]"]
  S30 = Pushbutton [package="[THT]"]
  S31 = Pushbutton [package="[THT]"]
  S32 = Pushbutton [package="[THT]"]
  S33 = Pushbutton [package="[THT]"]
  S34 = Pushbutton [package="[THT]"]
  S35 = Pushbutton [package="[THT]"]
  S36 = Pushbutton [package="[THT]"]
  U1 = 3.5mm Audio Jack [package=audio-jack-3.5mm-smd]

nets:
  N1: Mod1.pin_3, Mod1.pin_8, Mod1.pin_13, Mod1.pin_18, Mod1.pin_23, Mod1.pin_28, Mod1.pin_33, Mod1.pin_38, Mod1.pin_42, SW1.1, SW1.2, SW2.1, SW2.2, 元件1.GND, LCD1.pin2, U1.SLEEVE
  N2: Mod1.pin_5, U1.RIGHT
  N3: Mod1.pin_6, U1.LEFT
  N4: Mod1.pin_11, LCD1.pin_11
  N5: Mod1.pin_12, LCD1.pin_9
  N6: Mod1.pin_14, LCD1.pin_12
  N7: Mod1.pin_15, LCD1.pin_10
  N8: Mod1.pin_16, SW2.4
  N9: Mod1.pin_17, SW2.3
  N10: Mod1.pin_19, SW1.4
  N11: Mod1.pin_20, SW1.3
  N12: Mod1.pin_22, LCD1.pin3
  N13: Mod1.pin_24, LCD1.pin_7
  N14: Mod1.pin_25, LCD1.pin_6
  N15: Mod1.pin_26, LCD1.pin4
  N16: Mod1.pin_27, LCD1.pin_5
  N17: Mod1.pin_29, LCD1.pin_8
  N18: Mod1.pin_31, 元件1.A4
  N19: Mod1.pin_32, 元件1.A5
  N20: Mod1.pin_36, LCD1.pin_1
  N21: Mod1.pin_40, 元件1.5V
  N22: 元件1.D2, S1.Pin_3, S1.Pin_4, S2.Pin_3, S2.Pin_4, S3.Pin_3, S3.Pin_4, S4.Pin_3, S4.Pin_4, S5.Pin_3, S5.Pin_4, S6.Pin_3, S6.Pin_4
  N23: 元件1.D3, S7.Pin_3, S7.Pin_4, S8.Pin_3, S8.Pin_4, S9.Pin_3, S9.Pin_4, S10.Pin_3, S10.Pin_4, S11.Pin_3, S11.Pin_4, S12.Pin_3, S12.Pin_4
  N24: 元件1.D4, S13.Pin_3, S13.Pin_4, S14.Pin_3, S14.Pin_4, S15.Pin_3, S15.Pin_4, S16.Pin_3, S16.Pin_4, S17.Pin_3, S17.Pin_4, S18.Pin_3, S18.Pin_4
  N25: 元件1.D5, S19.Pin_3, S19.Pin_4, S20.Pin_3, S20.Pin_4, S21.Pin_3, S21.Pin_4, S22.Pin_3, S22.Pin_4, S23.Pin_3, S23.Pin_4, S24.Pin_3, S24.Pin_4
  N26: 元件1.D6, S25.Pin_3, S25.Pin_4, S26.Pin_3, S26.Pin_4, S27.Pin_3, S27.Pin_4, S28.Pin_3, S28.Pin_4, S29.Pin_3, S29.Pin_4, S30.Pin_3, S30.Pin_4
  N27: 元件1.D7, S31.Pin_3, S31.Pin_4, S32.Pin_3, S32.Pin_4, S33.Pin_3, S33.Pin_4, S34.Pin_3, S34.Pin_4, S35.Pin_3, S35.Pin_4, S36.Pin_3, S36.Pin_4
  N28: 元件1.D8, S1.Pin_1, S1.Pin_2, S7.Pin_1, S7.Pin_2, S13.Pin_1, S13.Pin_2, S19.Pin_1, S19.Pin_2, S25.Pin_1, S25.Pin_2, S31.Pin_1, S31.Pin_2
  N29: 元件1.D9, S2.Pin_1, S2.Pin_2, S8.Pin_1, S8.Pin_2, S14.Pin_1, S14.Pin_2, S20.Pin_1, S20.Pin_2, S26.Pin_1, S26.Pin_2, S32.Pin_1, S32.Pin_2
  N30: 元件1.D10, S3.Pin_1, S3.Pin_2, S9.Pin_1, S9.Pin_2, S15.Pin_1, S15.Pin_2, S21.Pin_1, S21.Pin_2, S27.Pin_1, S27.Pin_2, S33.Pin_1, S33.Pin_2
  N31: 元件1.D11/MOSI, S4.Pin_1, S4.Pin_2, S10.Pin_1, S10.Pin_2, S16.Pin_1, S16.Pin_2, S22.Pin_1, S22.Pin_2, S28.Pin_1, S28.Pin_2, S34.Pin_1, S34.Pin_2
  N32: 元件1.D12/MISO, S5.Pin_1, S5.Pin_2, S11.Pin_1, S11.Pin_2, S17.Pin_1, S17.Pin_2, S23.Pin_1, S23.Pin_2, S29.Pin_1, S29.Pin_2, S35.Pin_1, S35.Pin_2
  N33: 元件1.D13/SCK, S6.Pin_1, S6.Pin_2, S12.Pin_1, S12.Pin_2, S18.Pin_1, S18.Pin_2, S24.Pin_1, S24.Pin_2, S30.Pin_1, S30.Pin_2, S36.Pin_1, S36.Pin_2

notes:
  (nano) DO NOT PULL UP I2C!!!!!
  (pico) PULL UP!!!
  https://forum.arduino.cc/t/connecting-steval-mki197v1-3-3v-board-with-nano/644269/3

custom parts:
  Raspberry Pi Pico: Raspberry Pi Pico. Based around the RP2040 microcontroller the Pico is a low cost microcontroller device bringing Raspberry Pi quality, cost, and easy of use to the microcontroller space. Jan 2021, Split part in to two versions: tht (this one) and SMD. This one will drill holes for a .1 in header in pcb to allow plugging in the module as well as providing pads to solder the module to the top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
  TFT 1.8 inch 160x128 w SD: This is a generic 1.8 tft spi lcd display available on ebay and others. The 1.8" display has 128x160 color pixels.
